# Fritzing sketch Fritzing Sketch (saved by Fritzing 0.7.12b)
breadboards: 1

parts:
  Arduino1 = Arduino
  S5 = Pushbutton [package="[SMD]"]
  S6 = Pushbutton [package="[SMD]"]
  S7 = Pushbutton [package="[SMD]"]
  S8 = Pushbutton [package="[SMD]"]
  R1 = 68k Ω Resistor [package=THT]
  R2 = 10 Ω Resistor [package=THT]
  R5 = 47k Ω Resistor [package=THT]
  R3 = 15k Ω Resistor [package=THT]
  R4 = 68k Ω Resistor [package=THT]

nets:
  N1: Arduino1.GND, Arduino1.A0, R1.Pin_0, R1.Pin_1, R2.Pin_1, R5.Pin_1, R3.Pin_1, R4.Pin_1
  N2: Arduino1.+5V, S5.Pin_3, S5.Pin_4, S6.Pin_3, S6.Pin_4, S7.Pin_3, S7.Pin_4, S8.Pin_3, S8.Pin_4
  N3: S5.Pin_1, S5.Pin_2, R2.Pin_0
  N4: S6.Pin_1, S6.Pin_2, R3.Pin_0
  N5: S7.Pin_1, S7.Pin_2, R4.Pin_0
  N6: S8.Pin_1, S8.Pin_2, R5.Pin_0
